// Logisim project circuit.circ as structural Verilog: 11 circuits, main circuit main
module main (
  input  Reset,
  input  ResetRAM
);

  wire Clock, Clock_out, Cond, CTRL, Exec, Fetch, getcst_1_imm, Load, ramctrl_1_memload, ramctrl_1_memstore,
       Store, WriteReg;
  wire [2:0] GetOp;
  wire [15:0] Addr, alu_1_output, bit_extender_2_out, getcst_1_cst, JMP_Address, MemAddr, MemIN, PC, R0, R1,
       R2, R3, R4, R5, R6, R7, registres_1_out_sr2;
  wire [31:0] bit_extender_1_out, IR, MemOUT;

  Clock u_Clock (.out(Clock_out));
  Seq seq_1 (.ClockOrig(Clock_out), .reset(Reset), .Fetch(Fetch), .Exec(Exec), .Clock(Clock));
  LED led_1 (.in(Clock_out));
  RegPC regpc_1 (
    .JMP_Address(JMP_Address), .Cond(Cond), .CTRL(CTRL), .Exec(Exec), .Reset(Reset), .PC(PC), .Op(GetOp),
    .Clock(Clock));
  // Probe on PC
  GetAddr getaddr_1 (.PC(PC), .Addr(Addr), .Fetch(Fetch), .Load(Load), .MemAddr(MemAddr), .Store(Store));
  // Probe on Addr
  LED led_2 (.in(Fetch));
  LED led_3 (.in(Exec));
  assign bit_extender_1_out = {{16{MemIN[15]}}, MemIN};  // Bit_Extender bit_extender_1
  // Probe on MemIN
  // Probe on PC
  // Probe on IR
  DecodeIR decodeir_1 (
    .CTRL(CTRL), .WriteReg(WriteReg), .IR(IR), .Load(Load), .GetOp(GetOp), .JMPAddress(JMP_Address),
    .Store(Store));
  RamCtrl ramctrl_1 (
    .Store(Store), .Fetch(Fetch), .Exec(Exec), .Load(Load), .MemStore(ramctrl_1_memstore),
    .MemLoad(ramctrl_1_memload), .Clock(Clock));
  // Probe on MemOUT
  RAM #(.addrWidth(16), .dataWidth(32), .bus("separate")) ram_1 (
    .addr(Addr), .din(bit_extender_1_out), .data(MemOUT), .str(ramctrl_1_memstore), .clk(ramctrl_1_memstore),
    .ld(ramctrl_1_memload), .clr(ResetRAM));  // open: sel
  // Probe on R0
  // Probe on R3
  // Probe on R6
  Register #(.width(32), .trigger("falling")) RegIR (.D(MemOUT), .Q(IR), .clk(Fetch), .clr(Reset));  // open: en
  // Probe on R1
  // Probe on R4
  // Probe on R7
  // Probe on IR
  // Probe on R2
  // Probe on R5
  // Probe on IR[8:6]
  // Probe on IR[11:9]
  // Probe on IR[14:12]
  // Probe on getcst_1_cst
  GetCst getcst_1 (.IR(IR), .Cst(getcst_1_cst), .Imm(getcst_1_imm));
  Bit_Extender #(.in_width(32), .\type ("sign")) bit_extender_2 (.in(MemOUT), .out(bit_extender_2_out));
  Registres registres_1 (
    .SR1(IR[11:9]), .IN(alu_1_output), .SR2(IR[14:12]), .WriteReg(WriteReg), .DR(IR[8:6]), .OUT_SR1(MemAddr),
    .OUT_SR2(registres_1_out_sr2), .OUT_DR(MemIN), .R0(R0), .R1(R1), .R2(R2), .R3(R3), .R4(R4), .R5(R5),
    .R6(R6), .R7(R7), .Reset(Reset), .Clock(Exec), .MemIn(bit_extender_2_out), .LD(Load));
  // Probe on MemAddr
  ALU alu_1 (
    .Imm(getcst_1_imm), .e2(GetOp), .Input1(MemAddr), .Input2(registres_1_out_sr2), .Cst(getcst_1_cst),
    .Output(alu_1_output), .Clock(Exec));
  // Probe on alu_1_output
  // Probe on registres_1_out_sr2
  // Probe on R0
  // Probe on R1
  // Probe on R2
  // Probe on R3
  // Probe on R4
  // Probe on R5
  // Probe on R6
  // Probe on R7
  // Probe on alu_1_output
  Control control_1 (.RA(MemIN), .RB(MemAddr), .Operation(GetOp), .CTRL(CTRL), .Cond(Cond));

  // Notes on the sheet:
  //   RAM
endmodule

module DecodeIR (
  input  [31:0] IR,
  output WriteReg,
  output Store,
  output Load,
  output CTRL,
  output [2:0] GetOp,
  output [15:0] JMPAddress
);

  wire demultiplexer_1_out1;

  Demultiplexer #(.select(2), .disabled(0), .enable("false")) demultiplexer_1 (
    .out0(WriteReg), .out1(demultiplexer_1_out1), .out3(CTRL), .in(1'b1), .sel(IR[1:0]));  // open: out2
  Demultiplexer #(.select(3), .disabled(0)) demultiplexer_2 (
    .out0(Store), .out1(Load), .in(1'b1), .sel(IR[4:2]), .en(demultiplexer_1_out1));  // open: out2, out3, out4, out5, out6, out7

  assign GetOp = IR[4:2];
  assign JMPAddress = IR[27:12];
endmodule

module ALU (
  input  [15:0] Input1,
  input  [15:0] Input2,
  input  [15:0] Cst,
  input  Imm,
  input  Clock,
  input  [2:0] e2,
  output [15:0] Output
);

  wire [3:0] bit_extender_1_out;
  wire [15:0] adder_1_out, and_1_out, multiplexer_1_out, multiplier_1_out, or_1_out, shifter_1_out,
       shifter_2_out, subtractor_1_out, xor_1_out;

  Multiplexer #(.width(16), .enable("false")) multiplexer_1 (
    .in0(Input2), .in1(Cst), .out(multiplexer_1_out), .sel(Imm));
  Bit_Extender #(.in_width(16), .out_width(4), .\type ("input")) bit_extender_1 (
    .in(multiplexer_1_out), .out(bit_extender_1_out));  // open: extend
  Adder #(.width(16)) adder_1 (.a(Input1), .b(multiplexer_1_out), .out(adder_1_out));  // open: cin, cout
  Subtractor #(.width(16)) subtractor_1 (.a(Input1), .b(multiplexer_1_out), .out(subtractor_1_out));  // open: bin, bout
  Multiplier #(.width(16)) multiplier_1 (.a(Input1), .b(multiplexer_1_out), .out(multiplier_1_out));  // open: cin, cout
  assign and_1_out = Input1 & multiplexer_1_out;  // AND_Gate and_1, 16 bits wide
  assign or_1_out = Input1 | multiplexer_1_out;  // OR_Gate or_1, 16 bits wide
  assign xor_1_out = Input1 ^ multiplexer_1_out;  // XOR_Gate xor_1, 16 bits wide
  Shifter #(.width(16)) shifter_1 (.in(Input1), .\dist (bit_extender_1_out), .out(shifter_1_out));
  Shifter #(.width(16), .shift("lr")) shifter_2 (.in(Input1), .\dist (bit_extender_1_out), .out(shifter_2_out));
  Multiplexer #(.select(3), .width(16)) multiplexer_2 (
    .in0(adder_1_out), .in1(subtractor_1_out), .in2(multiplier_1_out), .in3(and_1_out), .in4(or_1_out),
    .in5(xor_1_out), .in6(shifter_1_out), .in7(shifter_2_out), .out(Output), .sel(e2), .en(Clock));
endmodule

module GetCst (
  input  [31:0] IR,
  output [15:0] Cst,
  output Imm
);

  Bit_Extender #(.in_width(20)) bit_extender_1 (.in(IR[31:12]), .out(Cst));

  assign Imm = IR[5];
endmodule

module GetAddr (
  input  [15:0] PC,
  input  [15:0] MemAddr,
  input  Load,
  input  Store,
  input  Fetch,
  output [15:0] Addr
);

  wire not_1_out, or_1_out, or_2_out;

  Multiplexer #(.width(16)) multiplexer_1 (.in0(PC), .in1(MemAddr), .out(Addr), .sel(not_1_out), .en(or_1_out));
  not not_1 (not_1_out, Fetch);
  or or_1 (or_1_out, Fetch, or_2_out);
  or or_2 (or_2_out, Load, Store);
endmodule

module RamCtrl (
  input  Clock,
  input  Exec,
  input  Fetch,
  input  Load,
  input  Store,
  output MemLoad,
  output MemStore
);

  wire and_1_out;

  and and_1 (and_1_out, Exec, Load);
  and and_2 (MemStore, Exec, Clock, Store);
  or or_1 (MemLoad, Fetch, and_1_out);
endmodule

module Registres (
  input  [15:0] IN,
  input  [15:0] MemIn,
  input  LD,
  input  [2:0] SR1,
  input  WriteReg,
  input  [2:0] SR2,
  input  [2:0] DR,
  input  Clock,
  input  Reset,
  output [15:0] R0,
  output [15:0] OUT_SR1,
  output [15:0] R1,
  output [15:0] R2,
  output [15:0] R3,
  output [15:0] OUT_SR2,
  output [15:0] R4,
  output [15:0] R5,
  output [15:0] R6,
  output [15:0] OUT_DR,
  output [15:0] R7
);

  wire decoder_1_out0, decoder_1_out1, decoder_1_out2, decoder_1_out3, decoder_1_out4, decoder_1_out5,
       decoder_1_out6, decoder_1_out7, or_1_out;
  wire [15:0] multiplexer_1_out;

  Multiplexer #(.width(16)) multiplexer_1 (.in0(IN), .in1(MemIn), .out(multiplexer_1_out), .sel(LD), .en(Clock));
  or or_1 (or_1_out, LD, WriteReg);
  Decoder #(.select(3), .disabled(0)) decoder_1 (
    .out0(decoder_1_out0), .out1(decoder_1_out1), .out2(decoder_1_out2), .out3(decoder_1_out3),
    .out4(decoder_1_out4), .out5(decoder_1_out5), .out6(decoder_1_out6), .out7(decoder_1_out7), .sel(DR),
    .en(or_1_out));
  Register #(.width(16), .trigger("falling")) u_R0 (
    .D(multiplexer_1_out), .en(decoder_1_out0), .Q(R0), .clk(Clock), .clr(Reset));
  Register #(.width(16), .trigger("falling")) u_R1 (
    .D(multiplexer_1_out), .en(decoder_1_out1), .Q(R1), .clk(Clock), .clr(Reset));
  Register #(.width(16), .trigger("falling")) u_R2 (
    .D(multiplexer_1_out), .en(decoder_1_out2), .Q(R2), .clk(Clock), .clr(Reset));
  Register #(.width(16), .trigger("falling")) u_R3 (
    .D(multiplexer_1_out), .en(decoder_1_out3), .Q(R3), .clk(Clock), .clr(Reset));
  Register #(.width(16), .trigger("falling")) u_R4 (
    .D(multiplexer_1_out), .en(decoder_1_out4), .Q(R4), .clk(Clock), .clr(Reset));
  Register #(.width(16), .trigger("falling")) u_R5 (
    .D(multiplexer_1_out), .en(decoder_1_out5), .Q(R5), .clk(Clock), .clr(Reset));
  Register #(.width(16), .trigger("falling")) u_R6 (
    .D(multiplexer_1_out), .en(decoder_1_out6), .Q(R6), .clk(Clock), .clr(Reset));
  Register #(.width(16), .trigger("falling")) u_R7 (
    .D(multiplexer_1_out), .en(decoder_1_out7), .Q(R7), .clk(Clock), .clr(Reset));
  Multiplexer #(.select(3), .width(16)) multiplexer_2 (
    .in0(R0), .in1(R1), .in2(R2), .in3(R3), .in4(R4), .in5(R5), .in6(R6), .in7(R7), .out(OUT_SR1), .sel(SR1),
    .en(Clock));
  Multiplexer #(.select(3), .width(16)) multiplexer_3 (
    .in0(R0), .in1(R1), .in2(R2), .in3(R3), .in4(R4), .in5(R5), .in6(R6), .in7(R7), .out(OUT_SR2), .sel(SR2),
    .en(Clock));
  Multiplexer #(.select(3), .width(16)) multiplexer_4 (
    .in0(R0), .in1(R1), .in2(R2), .in3(R3), .in4(R4), .in5(R5), .in6(R6), .in7(R7), .out(OUT_DR), .sel(DR),
    .en(Clock));
endmodule

module RegPC (
  input  [2:0] Op,
  input  [15:0] JMP_Address,
  input  Cond,
  input  CTRL,
  input  Exec,
  input  Reset,
  input  Clock,
  output [15:0] PC
);

  wire and_1_out, demultiplexer_1_out5, demultiplexer_1_out6;
  wire [15:0] adder_1_out, multiplexer_1_out, multiplexer_2_out, pile_1_addrout;

  Demultiplexer #(.select(3), .disabled(0)) demultiplexer_1 (
    .out5(demultiplexer_1_out5), .out6(demultiplexer_1_out6), .in(1'b1), .sel(Op), .en(CTRL));  // open: out0, out1, out2, out3, out4, out7
  Pile pile_1 (
    .Addr(adder_1_out), .CALL(demultiplexer_1_out5), .Exec(Exec), .RET(demultiplexer_1_out6), .Reset(Reset),
    .AddrOut(pile_1_addrout), .Clock(Clock));
  // Probe on pile_1_addrout
  Adder #(.width(16)) adder_1 (.a(PC), .b(16'h1), .out(adder_1_out));  // open: cin, cout
  Multiplexer #(.width(16), .enable("false")) multiplexer_1 (
    .in0(JMP_Address), .in1(pile_1_addrout), .out(multiplexer_1_out), .sel(demultiplexer_1_out6));
  and and_1 (and_1_out, Cond, CTRL);
  Multiplexer #(.width(16), .enable("false")) multiplexer_2 (
    .in0(adder_1_out), .in1(multiplexer_1_out), .out(multiplexer_2_out), .sel(and_1_out));
  // Probe on multiplexer_2_out
  Register #(.width(16), .trigger("falling")) u_PC (
    .D(multiplexer_2_out), .Q(PC), .clk(Exec), .clr(Reset));  // open: en
endmodule

module Seq (
  input  ClockOrig,
  input  reset,
  output Fetch,
  output Exec,
  output Clock
);

  Register #(.width(1), .trigger("falling")) register_1 (
    .D(Fetch), .Q(Exec), .clk(ClockOrig), .clr(reset));  // open: en
  not not_1 (Fetch, Exec);
  buf buffer_1 (Clock, ClockOrig);
endmodule

module Control (
  input  [15:0] RA,
  input  [15:0] RB,
  input  [2:0] Operation,
  input  CTRL,
  output Cond
);

  wire comparator_1_eq, comparator_1_gt, comparator_1_lt, not_1_out;

  Comparator #(.width(16)) comparator_1 (
    .a(RA), .b(RB), .gt(comparator_1_gt), .eq(comparator_1_eq), .lt(comparator_1_lt));
  not not_1 (not_1_out, comparator_1_eq);
  Multiplexer #(.select(3), .disabled(0)) multiplexer_1 (
    .in0(comparator_1_eq), .in1(comparator_1_lt), .in2(comparator_1_gt), .in3(not_1_out), .in4(1'b1),
    .in5(1'b1), .in6(1'b1), .out(Cond), .sel(Operation), .en(CTRL));  // open: in7
endmodule

module Pile (
  input  [15:0] Addr,
  input  CALL,
  input  RET,
  input  Clock,
  input  Exec,
  input  Reset,
  output [15:0] AddrOut
);

  wire and_1_out, or_1_out;
  wire [23:0] adder_1_out, multiplexer_1_out, register_1_q, subtractor_1_out;

  Adder #(.width(24)) adder_1 (.a(register_1_q), .b(24'h1), .out(adder_1_out));  // open: cin, cout
  Subtractor #(.width(24)) subtractor_1 (.a(register_1_q), .b(24'h1), .out(subtractor_1_out));  // open: bin, bout
  // Probe on subtractor_1_out
  or or_1 (or_1_out, CALL, RET);
  // Probe on adder_1_out
  // Probe on multiplexer_1_out
  Multiplexer #(.width(24), .enable("false")) multiplexer_1 (
    .in0(adder_1_out), .in1(subtractor_1_out), .out(multiplexer_1_out), .sel(RET));
  and and_1 (and_1_out, or_1_out, Clock, Exec);
  Register #(.width(24)) register_1 (
    .D(multiplexer_1_out), .Q(register_1_q), .clk(and_1_out), .clr(Reset));  // open: en
  RAM #(.addrWidth(24), .dataWidth(16), .bus("separate")) ram_1 (
    .addr(register_1_q), .din(Addr), .data(AddrOut), .str(CALL), .sel(and_1_out), .clk(and_1_out), .ld(RET),
    .clr(Reset));
endmodule
